# Fritzing sketch Final Board (saved by Fritzing 0.9.2b)
breadboards: 2

parts:
  U1 = CNZ1120 [package=cnz1120]
  U2 = CNZ1120 [package=cnz1120]
  R1 = Resistor [tolerance=±5% resistance=220 package=THT]
  R2 = Resistor [tolerance=±5% resistance=220 package=THT]
  R3 = Resistor [tolerance=±5% resistance=220 package=THT]
  R4 = Resistor [tolerance=±5% resistance=220 package=THT]
  R5 = Resistor [tolerance=±5% resistance=220 package=THT]
  NEOPIXEL4 = Neopixel Strip -- White (30/m)
  NEOPIXEL5 = Neopixel Strip -- White (30/m)
  NEOPIXEL6 = Neopixel Strip -- White (30/m)
  NEOPIXEL7 = Neopixel Strip -- White (30/m)
  NEOPIXEL8 = Neopixel Strip -- White (30/m)
  NEOPIXEL9 = Neopixel Strip -- White (30/m)
  NEOPIXEL10 = Neopixel Strip -- White (30/m)
  NEOPIXEL11 = Neopixel Strip -- White (30/m)
  NEOPIXEL12 = Neopixel Strip -- White (30/m)
  NEOPIXEL13 = Neopixel Strip -- White (30/m)
  NEOPIXEL14 = Neopixel Strip -- White (30/m)
  NEOPIXEL15 = Neopixel Strip -- White (30/m)
  C1 = Electrolytic Capacitor [capacitance=47µF package="1010 [SMD, electrolytic]"]
  R6 = Resistor [tolerance=±5% resistance=220 package=THT]
  R7 = Resistor [tolerance=±5% resistance=220 package=THT]
  R8 = Resistor [tolerance=±5% resistance=220 package=THT]
  R9 = Resistor [tolerance=±5% resistance=10k package="0402 [SMD]"]
  R10 = Resistor [tolerance=±5% resistance=10k package="0402 [SMD]"]
  ARDUINO1 = Arduino Micro

nets:
  N1: U1.1, R2.Pin_0
  GND: U1.2, U2.2, NEOPIXEL4.GND, NEOPIXEL5.GND, NEOPIXEL6.GND, NEOPIXEL7.GND, NEOPIXEL8.GND, NEOPIXEL9.GND, NEOPIXEL10.GND, NEOPIXEL11.GND, NEOPIXEL12.GND, NEOPIXEL13.GND, NEOPIXEL14.GND, NEOPIXEL15.GND, C1.-, R9.Pin_0, R10.Pin_0, ARDUINO1.GND#6
  +5V: U1.3, U2.3, R1.Pin_1, R2.Pin_1, NEOPIXEL4.+5V, NEOPIXEL5.+5V, NEOPIXEL6.+5V, NEOPIXEL7.+5V, NEOPIXEL8.+5V, NEOPIXEL9.+5V, NEOPIXEL10.+5V, NEOPIXEL11.+5V, NEOPIXEL12.+5V, NEOPIXEL13.+5V, NEOPIXEL14.+5V, NEOPIXEL15.+5V, C1.+, ARDUINO1.5V
  N2: U1.4, R9.Pin_1, ARDUINO1.D9
  N3: U2.1, R1.Pin_0
  N4: U2.4, R10.Pin_1, ARDUINO1.D5
  N5: R3.Pin_0, ARDUINO1.D8
  N6: R3.Pin_1, NEOPIXEL10.Din, NEOPIXEL15.Din
  N7: R4.Pin_0, ARDUINO1.D6
  N8: R4.Pin_1, NEOPIXEL4.Din, NEOPIXEL5.Din
  N9: R5.Pin_0, ARDUINO1.D7
  N10: R5.Pin_1, NEOPIXEL9.Din, NEOPIXEL13.Din
  N11: NEOPIXEL6.Din, NEOPIXEL7.Din, R6.Pin_0
  N12: NEOPIXEL8.Din, NEOPIXEL12.Din, R7.Pin_0
  N13: NEOPIXEL11.Din, NEOPIXEL14.Din, R8.Pin_0
  N14: R6.Pin_1, ARDUINO1.D10
  N15: R7.Pin_1, ARDUINO1.D11
  N16: R8.Pin_1, ARDUINO1.D12

custom parts:
  Neopixel Strip -- White (30/m): These NeoPixel strips have 30 digitally-addressable pixel LEDs per meter and are very affordable and are only 12.5 mm wide, 10 mm if you remove the strip from the casing.
  Arduino Micro: Arduino Micro Microcontroller
